# Fritzing sketch 基本電路_LCD2004_按鈕開燈 (saved by Fritzing 0.9.2b)
breadboards: 1

parts:
  Ameba1 = Ameba
  Grove1 = Grove Button
  R1 = Resistor [tolerance=±5% resistance=220 package=THT]
  LED1 = LED - 5mm [color="Red (633nm)" package="5 mm [THT]"]
  LCM1602_IIC4 = LCM1602 IIC [part_number="LCM1602 IIC" chip_label="LCM1602 IIC" package="DIP (Dual Inline) [THT]"]
  LCD5 = LCD 20x04

nets:
  N1: Ameba1.D7, Grove1.SIG
  N2: Ameba1.D13, LED1.anode
  GND: Ameba1.GND, Grove1.GND, R1.Pin_0, LCM1602_IIC4.GND
  VCC: Ameba1.5V, Grove1.VCC, LCM1602_IIC4.VCC
  N3: R1.Pin_1, LED1.cathode
  VSS: LCM1602_IIC4.VSS, LCD5.VSS
  VDD: LCM1602_IIC4.VDD, LCD5.VDD
  N4: LCM1602_IIC4.V0, LCD5.V0
  N5: LCM1602_IIC4.RS, LCD5.RS
  N6: LCM1602_IIC4.RW, LCD5.R/W
  N7: LCM1602_IIC4.E, LCD5.E
  N8: LCM1602_IIC4.D0, LCD5.DB0
  N9: LCM1602_IIC4.D1, LCD5.DB1
  N10: LCM1602_IIC4.D2, LCD5.DB2
  N11: LCM1602_IIC4.D3, LCD5.DB3
  N12: LCM1602_IIC4.D4, LCD5.DB4
  N13: LCM1602_IIC4.D5, LCD5.DB5
  N14: LCM1602_IIC4.D6, LCD5.DB6
  N15: LCM1602_IIC4.D7, LCD5.DB7
  N16: LCM1602_IIC4.A, LCD5.LED+
  N17: LCM1602_IIC4.K, LCD5.LED-
  N18: LCM1602_IIC4.LED_A, LCM1602_IIC4.LED_B

notes:
  D13
  D7
  LED +5V
  D13
  GND
  LED GND
  220 Ω

custom parts:
  Ameba: Ameba EVB
  LCM1602 IIC: I2C-Module to use a 1602 or 2004 LCD on with the wire.h libory Serial LCD Modul
  LCD 20x04: LCD character display, 20 characters by 4 rows. Green.
